// Logisim project Projeto Final - Circuitos.circ as structural Verilog: 4 circuits, main circuit MCAgua
module MCAgua (
  input  SNA,
  input  STA,
  input  AMCA,
  output VA,
  output RAQ,
  output DMCA
);

  wire and_1_out, and_2_out, and_3_out, and_4_out, clock_1_out, or_1_out, or_2_out, T0_q, T0_qn, T1_q, T1_qn;

  Clock clock_1 (.out(clock_1_out));
  and and_1 (and_1_out, T0_q, T1_q);
  and and_2 (and_2_out, SNA, T0_q);
  or or_1 (or_1_out, and_1_out, and_2_out);
  T_Flip_Flop T1 (.clk(clock_1_out), .T(or_1_out), .Q(T1_q), .Qn(T1_qn));  // open: preset, reset, en
  and and_3 (and_3_out, T1_q, STA);
  or or_2 (or_2_out, DMCA, and_4_out, and_2_out, and_3_out);
  T_Flip_Flop T0 (.clk(clock_1_out), .T(or_2_out), .Q(T0_q), .Qn(T0_qn));  // open: preset, reset, en
  and and_4 (and_4_out, AMCA, T0_qn, T1_qn);
  and and_5 (VA, T0_q, T1_qn);
  and and_6 (RAQ, T0_qn, T1_q);
  and and_7 (DMCA, T0_q, T1_q);
endmodule

module MCLavagem (
  input  DMCA,
  input  SNA,
  output MD,
  output ME,
  output BA,
  output MC_BA,
  output DMCL
);

  wire and_1_out, and_2_out, and_3_out, and_4_out, and_5_out, and_6_out, and_7_out, and_8_out, and_9_out,
       and_10_out, and_11_out, clock_1_out, not_1_out, not_2_out, not_3_out, or_1_out, or_2_out, T0_q, T0_qn,
       T1_q, T1_qn, T2_q, T2_qn;

  Clock clock_1 (.out(clock_1_out));
  not not_1 (not_1_out, SNA);
  and and_1 (and_1_out, T2_qn, T0_q);
  and and_2 (and_2_out, not_1_out, T0_q);
  and and_3 (and_3_out, not_1_out, DMCA);
  and and_4 (and_4_out, DMCA, SNA, T2_qn);
  and and_5 (and_5_out, T2_qn, T0_q);
  not not_2 (not_2_out, DMCA);
  not not_3 (not_3_out, SNA);
  and and_6 (and_6_out, not_2_out, not_3_out, T2_q);
  and and_7 (and_7_out, T1_q, T0_q);
  or or_1 (or_1_out, and_7_out, and_1_out, and_2_out);
  or or_2 (or_2_out, T1_q, and_3_out, and_4_out, and_5_out, and_6_out, and_11_out);
  T_Flip_Flop T2 (.clk(clock_1_out), .T(and_7_out), .Q(T2_q), .Qn(T2_qn));  // open: preset, reset, en
  T_Flip_Flop T1 (.clk(clock_1_out), .T(or_1_out), .Q(T1_q), .Qn(T1_qn));  // open: preset, reset, en
  T_Flip_Flop T0 (.clk(clock_1_out), .T(or_2_out), .Q(T0_q), .Qn(T0_qn));  // open: preset, reset, en
  and and_8 (and_8_out, T0_qn, T1_q, T2_qn);
  and and_9 (and_9_out, T2_qn, T1_qn, T0_q);
  or or_3 (MD, and_8_out, and_9_out);
  and and_10 (and_10_out, T2_qn, T1_q, T0_q);
  or or_4 (ME, and_10_out, and_11_out);
  and and_11 (and_11_out, T2_q, T1_qn, T0_qn);
  and and_12 (BA, T2_q, T1_qn, T0_q);
  and and_13 (MC_BA, T2_q, T1_q, T0_qn);
  and and_14 (DMCL, T2_q, T1_q, T0_q);
endmodule

module MCMaquina (
  input  DMCA,
  input  DMCL,
  input  BI,
  output AMCA,
  output AMCL
);

  wire and_1_out, and_2_out, and_3_out, clock_1_out, or_1_out, or_2_out, X0_q, X0_qn, X1_q, X1_qn;

  Clock clock_1 (.out(clock_1_out));
  and and_1 (and_1_out, X1_qn, DMCA, X0_q);
  and and_2 (and_2_out, X1_q, DMCL, X0_qn);
  and and_3 (and_3_out, X0_qn, BI, X1_qn);
  or or_1 (or_1_out, and_1_out, and_2_out);
  or or_2 (or_2_out, and_1_out, and_3_out);
  T_Flip_Flop X1 (.clk(clock_1_out), .T(or_1_out), .Q(X1_q), .Qn(X1_qn));  // open: preset, reset, en
  T_Flip_Flop X0 (.clk(clock_1_out), .T(or_2_out), .Q(X0_q), .Qn(X0_qn));  // open: preset, reset, en
  and and_4 (AMCA, X1_qn, X0_q);
  and and_5 (AMCL, X1_q, X0_qn);
endmodule

module MAaquina_de_lavar (
  input  SNA,
  input  STA,
  input  BI,
  output MD,
  output ME,
  output BA,
  output MC_BA,
  output VA,
  output RAQ
);

  wire mcagua_1_dmca, mclavagem_1_dmcl, mcmaquina_1_amca;

  MCMaquina mcmaquina_1 (
    .DMCA(mcagua_1_dmca), .DMCL(mclavagem_1_dmcl), .BI(BI), .AMCA(mcmaquina_1_amca));  // open: AMCL
  MCAgua mcagua_1 (.SNA(SNA), .STA(STA), .AMCA(mcmaquina_1_amca), .VA(VA), .RAQ(RAQ), .DMCA(mcagua_1_dmca));
  MCLavagem mclavagem_1 (
    .DMCA(mcagua_1_dmca), .SNA(SNA), .MD(MD), .ME(ME), .BA(BA), .MC_BA(MC_BA), .DMCL(mclavagem_1_dmcl));
endmodule
